// Logisim project proj.circ as structural Verilog: 3 circuits, main circuit main
module main (
  input  [31:0] in_1
);

  wire button_1_out;
  wire [4:0] counter_1_q;
  wire [31:0] map_1_p3, map_1_p4, map_1_p5, map_1_p6, map_1_p7, map_1_p8, map_1_p9, map_1_p10, map_1_p11,
       map_1_p12, map_1_p13, map_1_p14, map_1_p15, map_1_p16, map_1_p17, map_1_p18, map_1_p19, map_1_p20,
       map_1_p21, map_1_p22, map_1_p23, map_1_p24, map_1_p25, map_1_p26, map_1_p27, map_1_p28, map_1_p29,
       map_1_p30, map_1_p31, map_1_p32, map_1_p33, map_1_p34;

  Button button_1 (.out(button_1_out));
  Counter #(.width(5), .max('h1f)) counter_1 (.Q(counter_1_q), .clk(button_1_out));  // open: load, D, count, carry, clr
  DotMatrix #(.inputtype("row"), .matrixcols(32), .matrixrows(32)) dotmatrix_1 (
    .row0(map_1_p3), .row1(map_1_p4), .row2(map_1_p5), .row3(map_1_p6), .row4(map_1_p7), .row5(map_1_p8),
    .row6(map_1_p9), .row7(map_1_p10), .row8(map_1_p11), .row9(map_1_p12), .row10(map_1_p13),
    .row11(map_1_p14), .row12(map_1_p15), .row13(map_1_p16), .row14(map_1_p17), .row15(map_1_p18),
    .row16(map_1_p19), .row17(map_1_p20), .row18(map_1_p21), .row19(map_1_p22), .row20(map_1_p23),
    .row21(map_1_p24), .row22(map_1_p25), .row23(map_1_p26), .row24(map_1_p27), .row25(map_1_p28),
    .row26(map_1_p29), .row27(map_1_p30), .row28(map_1_p31), .row29(map_1_p32), .row30(map_1_p33),
    .row31(map_1_p34));
  // map map_1: pin names not known; wires that end beside it: counter_1_q, in_1, map_1_p3, map_1_p4, map_1_p5, map_1_p6, map_1_p7, map_1_p8, map_1_p9, map_1_p10, map_1_p11, map_1_p12, map_1_p13, map_1_p14, map_1_p15, map_1_p16, map_1_p17, map_1_p18, map_1_p19, map_1_p20, map_1_p21, map_1_p22, map_1_p23, map_1_p24, map_1_p25, map_1_p26, map_1_p27, map_1_p28, map_1_p29, map_1_p30, map_1_p31, map_1_p32, map_1_p33, map_1_p34
endmodule

module map (
  input  [4:0] in_1,
  input  [31:0] in_2,
  input  [4:0] in_3,
  output [31:0] out_4,
  output [31:0] out_5,
  output [31:0] out_6,
  output [31:0] out_7,
  output [31:0] out_8,
  output [31:0] out_9,
  output [31:0] out_10,
  output [31:0] out_11,
  output [31:0] out_12,
  output [31:0] out_13,
  output [31:0] out_14,
  output [31:0] out_15,
  output [31:0] out_16,
  output [31:0] out_17,
  output [31:0] out_18,
  output [31:0] out_19,
  output [31:0] out_20,
  output [31:0] out_21,
  output [31:0] out_22,
  output [31:0] out_23,
  output [31:0] out_24,
  output [31:0] out_25,
  output [31:0] out_26,
  output [31:0] out_27,
  output [31:0] out_28,
  output [31:0] out_29,
  output [31:0] out_30,
  output [31:0] out_31,
  output [31:0] out_32,
  output [31:0] out_33,
  output [31:0] out_34,
  output [31:0] out_35
);

  wire [31:0] demultiplexer_1_out0, demultiplexer_1_out1, demultiplexer_1_out2, demultiplexer_1_out3,
       demultiplexer_1_out4, demultiplexer_1_out5, demultiplexer_1_out6, demultiplexer_1_out7,
       demultiplexer_1_out8, demultiplexer_1_out9, demultiplexer_1_out10, demultiplexer_1_out11,
       demultiplexer_1_out12, demultiplexer_1_out13, demultiplexer_1_out14, demultiplexer_1_out15,
       demultiplexer_1_out16, demultiplexer_1_out17, demultiplexer_1_out18, demultiplexer_1_out19,
       demultiplexer_1_out20, demultiplexer_1_out21, demultiplexer_1_out22, demultiplexer_1_out23,
       demultiplexer_1_out24, demultiplexer_1_out25, demultiplexer_1_out26, demultiplexer_1_out27,
       demultiplexer_1_out28, demultiplexer_1_out29, demultiplexer_1_out30, demultiplexer_1_out31,
       shifter_1_out;

  Shifter #(.width(32), .shift("rl")) shifter_1 (.in(in_2), .\dist (in_3), .out(shifter_1_out));
  Demultiplexer #(.select(5), .width(32), .enable("false")) demultiplexer_1 (
    .out0(demultiplexer_1_out0), .out1(demultiplexer_1_out1), .out2(demultiplexer_1_out2),
    .out3(demultiplexer_1_out3), .out4(demultiplexer_1_out4), .out5(demultiplexer_1_out5),
    .out6(demultiplexer_1_out6), .out7(demultiplexer_1_out7), .out8(demultiplexer_1_out8),
    .out9(demultiplexer_1_out9), .out10(demultiplexer_1_out10), .out11(demultiplexer_1_out11),
    .out12(demultiplexer_1_out12), .out13(demultiplexer_1_out13), .out14(demultiplexer_1_out14),
    .out15(demultiplexer_1_out15), .out16(demultiplexer_1_out16), .out17(demultiplexer_1_out17),
    .out18(demultiplexer_1_out18), .out19(demultiplexer_1_out19), .out20(demultiplexer_1_out20),
    .out21(demultiplexer_1_out21), .out22(demultiplexer_1_out22), .out23(demultiplexer_1_out23),
    .out24(demultiplexer_1_out24), .out25(demultiplexer_1_out25), .out26(demultiplexer_1_out26),
    .out27(demultiplexer_1_out27), .out28(demultiplexer_1_out28), .out29(demultiplexer_1_out29),
    .out30(demultiplexer_1_out30), .out31(demultiplexer_1_out31), .in(shifter_1_out), .sel(in_1));
  // Probe on shifter_1_out
  assign out_4 = {32{1'b0}} | demultiplexer_1_out0;  // OR_Gate or_1, 32 bits wide
  assign out_5 = {32{1'b0}} | demultiplexer_1_out1;  // OR_Gate or_2, 32 bits wide
  assign out_6 = {32{1'b0}} | demultiplexer_1_out2;  // OR_Gate or_3, 32 bits wide
  assign out_7 = {32{1'b0}} | demultiplexer_1_out3;  // OR_Gate or_4, 32 bits wide
  assign out_8 = {32{1'b0}} | demultiplexer_1_out4;  // OR_Gate or_5, 32 bits wide
  assign out_9 = {32{1'b0}} | demultiplexer_1_out5;  // OR_Gate or_6, 32 bits wide
  assign out_10 = {32{1'b0}} | demultiplexer_1_out6;  // OR_Gate or_7, 32 bits wide
  assign out_11 = {32{1'b0}} | demultiplexer_1_out7;  // OR_Gate or_8, 32 bits wide
  assign out_12 = {32{1'b0}} | demultiplexer_1_out8;  // OR_Gate or_9, 32 bits wide
  assign out_13 = {32{1'b0}} | demultiplexer_1_out9;  // OR_Gate or_10, 32 bits wide
  assign out_14 = {32{1'b0}} | demultiplexer_1_out10;  // OR_Gate or_11, 32 bits wide
  assign out_15 = {32{1'b0}} | demultiplexer_1_out11;  // OR_Gate or_12, 32 bits wide
  assign out_16 = {32{1'b0}} | demultiplexer_1_out12;  // OR_Gate or_13, 32 bits wide
  assign out_17 = {32{1'b0}} | demultiplexer_1_out13;  // OR_Gate or_14, 32 bits wide
  assign out_18 = {32{1'b0}} | demultiplexer_1_out14;  // OR_Gate or_15, 32 bits wide
  assign out_19 = {32{1'b0}} | demultiplexer_1_out15;  // OR_Gate or_16, 32 bits wide
  assign out_20 = {32{1'b0}} | demultiplexer_1_out16;  // OR_Gate or_17, 32 bits wide
  assign out_21 = {32{1'b0}} | demultiplexer_1_out17;  // OR_Gate or_18, 32 bits wide
  assign out_22 = {32{1'b0}} | demultiplexer_1_out18;  // OR_Gate or_19, 32 bits wide
  assign out_23 = {32{1'b0}} | demultiplexer_1_out19;  // OR_Gate or_20, 32 bits wide
  assign out_24 = {32{1'b0}} | demultiplexer_1_out20;  // OR_Gate or_21, 32 bits wide
  assign out_25 = {32{1'b0}} | demultiplexer_1_out21;  // OR_Gate or_22, 32 bits wide
  assign out_26 = {32{1'b0}} | demultiplexer_1_out22;  // OR_Gate or_23, 32 bits wide
  assign out_27 = {32{1'b0}} | demultiplexer_1_out23;  // OR_Gate or_24, 32 bits wide
  assign out_28 = {32{1'b0}} | demultiplexer_1_out24;  // OR_Gate or_25, 32 bits wide
  assign out_29 = {32{1'b0}} | demultiplexer_1_out25;  // OR_Gate or_26, 32 bits wide
  assign out_30 = {32{1'b0}} | demultiplexer_1_out26;  // OR_Gate or_27, 32 bits wide
  assign out_31 = {32{1'b0}} | demultiplexer_1_out27;  // OR_Gate or_28, 32 bits wide
  assign out_32 = {32{1'b0}} | demultiplexer_1_out28;  // OR_Gate or_29, 32 bits wide
  assign out_33 = {32{1'b0}} | demultiplexer_1_out29;  // OR_Gate or_30, 32 bits wide
  assign out_34 = {32{1'b0}} | demultiplexer_1_out30;  // OR_Gate or_31, 32 bits wide
  assign out_35 = {32{1'b0}} | demultiplexer_1_out31;  // OR_Gate or_32, 32 bits wide
endmodule

module isW (
  output out_1
);

  wire comparator_1_eq, comparator_2_eq;
  wire [6:0] keyboard_1_data;

  Keyboard keyboard_1 (.clk(1'b1), .data(keyboard_1_data));  // open: re, clr, avail
  Comparator #(.width(7)) comparator_1 (.a(7'b1010111), .b(keyboard_1_data), .eq(comparator_1_eq));  // open: gt, lt
  Comparator #(.width(7)) comparator_2 (.a(keyboard_1_data), .b(7'b1110111), .eq(comparator_2_eq));  // open: gt, lt
  or or_1 (out_1, comparator_1_eq, comparator_2_eq);
endmodule
